// Logisim project Cache.circ as structural Verilog: 5 circuits, main circuit implementation
module implementation (
  input  [9:0] CpuAddressIn,
  input  CpuReadIn,
  input  CpuWriteIn,
  input  [7:0] CpuWriteValueIn,
  input  [31:0] LineFromMemIn,
  input  ClkIn,
  output ReadyOut,
  output DidContainOut,
  output [7:0] ByteReadOut,
  output [7:0] MemAddressOut,
  output MemReadOut,
  output MemWriteOut,
  output [31:0] Line2MemOut
);

  wire and_1_out, contains0, contains1, CpuRead, CpuWrite, demultiplexer_1_out0, demultiplexer_1_out1,
       Initialize, OlderTagDirty, OlderTagDirty0, OlderTagDirty1, RealDidContain, S0, S1, S2, UpdateAges,
       UpdateAges0, UpdateAges1, WayWriteEnable, WayWriteEnable0, WayWriteEnable1, WriteFrom;
  wire [1:0] CPUOffsetBitsSet0, CPUOffsetBitsSet1;
  wire [2:0] next_state_fsm_1_s0_next;
  wire [6:0] CPUTagBitsSet0, CPUTagBitsSet1, multiplexer_6_out, OlderTag0, OlderTag1;
  wire [7:0] ByteReadOut0, ByteReadOut1, CpuWriteValue, CPUWriteValue0, CPUWriteValue1;
  wire [9:0] CpuAddress;
  wire [31:0] BlockFromMemSet0, BlockFromMemSet1, OlderBlock0, OlderBlock1;

  Register #(.width(10)) u_CPUAddress (.D(CpuAddressIn), .en(ReadyOut), .clk(ClkIn), .Q(CpuAddress));  // open: clr
  Register CPUValueIn (.D(CpuWriteValueIn), .en(ReadyOut), .clk(ClkIn), .Q(CpuWriteValue));  // open: clr
  // Probe on CpuAddress
  Register #(.width(1)) u_CPURead (.D(CpuReadIn), .en(ReadyOut), .clk(ClkIn), .Q(CpuRead));  // open: clr
  Register #(.width(1)) u_CPUWrite (.D(CpuWriteIn), .en(ReadyOut), .clk(ClkIn), .Q(CpuWrite));  // open: clr
  // Probe on CpuWriteValue
  Next_State_FSM next_state_fsm_1 (
    .S2(S2), .S1(S1), .S0(S0), .CpuRead(CpuRead), .CpuWrite(CpuWrite), .DidContain(RealDidContain),
    .OlderTagDirty(OlderTagDirty), .S2_Next(next_state_fsm_1_s0_next[2]),
    .S1_Next(next_state_fsm_1_s0_next[1]), .S0_Next(next_state_fsm_1_s0_next[0]));
  Register #(.width(3)) register_1 (.D(next_state_fsm_1_s0_next), .clk(ClkIn), .Q({S2, S1, S0}));  // open: en, clr
  FSM_Output fsm_output_1 (
    .S2(S2), .S1(S1), .S0(S0), .CpuRead(CpuRead), .CpuWrite(CpuWrite), .DidContain(DidContainOut),
    .OlderTagDirty(OlderTagDirty), .Initialize(Initialize), .Ready(ReadyOut), .MemRead(MemReadOut),
    .MemWrite(MemWriteOut), .WayWriteEnable(WayWriteEnable), .WriteFrom(WriteFrom), .UpdateAges(UpdateAges));
  Demultiplexer #(.enable("false")) demultiplexer_1 (
    .out0(demultiplexer_1_out0), .out1(demultiplexer_1_out1), .in(UpdateAges), .sel(CpuAddress[2]));
  Demultiplexer #(.enable("false"), .width(7)) demultiplexer_2 (
    .out0(CPUTagBitsSet0), .out1(CPUTagBitsSet1), .in(CpuAddress[9:3]), .sel(CpuAddress[2]));
  Demultiplexer #(.enable("false"), .width(2)) demultiplexer_3 (
    .out0(CPUOffsetBitsSet0), .out1(CPUOffsetBitsSet1), .in(CpuAddress[1:0]), .sel(CpuAddress[2]));
  Demultiplexer #(.enable("false"), .width(32)) demultiplexer_4 (
    .out0(BlockFromMemSet0), .out1(BlockFromMemSet1), .in(LineFromMemIn), .sel(CpuAddress[2]));
  Demultiplexer #(.enable("false"), .width(8)) demultiplexer_5 (
    .out0(CPUWriteValue0), .out1(CPUWriteValue1), .in(CpuWriteValue), .sel(CpuAddress[2]));
  Demultiplexer #(.enable("false")) demultiplexer_6 (
    .out0(WayWriteEnable0), .out1(WayWriteEnable1), .in(WayWriteEnable), .sel(CpuAddress[2]));
  Multiplexer #(.enable("false")) multiplexer_1 (
    .in0(demultiplexer_1_out0), .in1(1'b1), .out(UpdateAges0), .sel(Initialize));
  Multiplexer #(.enable("false")) multiplexer_2 (
    .in0(demultiplexer_1_out1), .in1(1'b1), .out(UpdateAges1), .sel(Initialize));
  Set Set0 (
    .ClkIn(ClkIn), .InitIn(Initialize), .CPUTag(CPUTagBitsSet0), .CPUOffset(CPUOffsetBitsSet0),
    .BlockFromMem(BlockFromMemSet0), .CPUValue(CPUWriteValue0), .WriteFrom(WriteFrom),
    .WayWriteEnable(WayWriteEnable0), .UpdateAgesEnable(UpdateAges0), .contains(contains0),
    .ByteReadOut(ByteReadOut0), .OlderTagOut(OlderTag0), .OlderTagDirtyOut(OlderTagDirty0),
    .OlderBlockOut(OlderBlock0));
  Set Set1 (
    .ClkIn(ClkIn), .InitIn(Initialize), .CPUTag(CPUTagBitsSet1), .CPUOffset(CPUOffsetBitsSet1),
    .BlockFromMem(BlockFromMemSet1), .CPUValue(CPUWriteValue1), .WriteFrom(WriteFrom),
    .WayWriteEnable(WayWriteEnable1), .UpdateAgesEnable(UpdateAges1), .contains(contains1),
    .ByteReadOut(ByteReadOut1), .OlderTagOut(OlderTag1), .OlderTagDirtyOut(OlderTagDirty1),
    .OlderBlockOut(OlderBlock1));
  Multiplexer #(.enable("false")) multiplexer_3 (
    .in0(contains0), .in1(contains1), .out(RealDidContain), .sel(CpuAddress[2]));
  and and_1 (and_1_out, ~S2, S1, ~S0);  // AND_Gate
  Multiplexer #(.enable("false"), .width(8)) multiplexer_4 (
    .in0(ByteReadOut0), .in1(ByteReadOut1), .out(ByteReadOut), .sel(CpuAddress[2]));
  Multiplexer #(.enable("false")) multiplexer_5 (
    .in0(OlderTagDirty0), .in1(OlderTagDirty1), .out(OlderTagDirty), .sel(CpuAddress[2]));
  Multiplexer #(.enable("false"), .width(7)) multiplexer_6 (
    .in0(OlderTag0), .in1(OlderTag1), .out(multiplexer_6_out), .sel(CpuAddress[2]));
  // Probe on CpuAddress[9:2]
  Multiplexer #(.enable("false"), .width(32)) multiplexer_7 (
    .in0(OlderBlock0), .in1(OlderBlock1), .out(Line2MemOut), .sel(CpuAddress[2]));
  Register #(.width(1)) register_2 (.D(RealDidContain), .en(and_1_out), .clk(ClkIn), .Q(DidContainOut));  // open: clr
  // Probe on ByteReadOut
  Multiplexer #(.enable("false"), .select(2), .width(8)) multiplexer_8 (
    .in1({multiplexer_6_out, CpuAddress[2]}), .in2(CpuAddress[9:2]), .out(MemAddressOut),
    .sel({MemReadOut, MemWriteOut}));  // open: in0, in3

  // Other names for the same wires on the sheet: SetBit = CpuAddress[2]; MemWrite = MemWriteOut; MemRead = MemReadOut;
  //   clk = ClkIn; CPUOffsetBits[1:0] = CpuAddress[1:0]; CPUTagBits[6:0] = CpuAddress[9:3];
  //   DidContain = DidContainOut; LineFromMem[31:0] = LineFromMemIn; MemAddress[7:0] = MemAddressOut;
  //   Ready = ReadyOut; ByteRead[7:0] = ByteReadOut; SelectedSetByteRead[7:0] = ByteReadOut;
  //   Line2Mem[31:0] = Line2MemOut; SelectedSetLine2Mem[31:0] = Line2MemOut

  // Notes on the sheet:
  //   0->MemRead from MemAddress; 1->MemWrite Line2Mem at MemAddress, then MemRead
  //   FSM - Input`s
  //   FSM - Output`s
  //   FSM -Out; Will initialize the ages within a set; 0 - do not initialize; 1 - initialize
  //   1-if we need to read from CPU or Memory; 0 -otherwise.
  //   1-from CPU; 0-from Memory. Probably will be handled by the FSM
  //   1-when ((CpuRead=1 OR CpuWrite=1) AND DidContain=1) OR Initialize =1; 0-otherwise;
  //   VLADIMIR PLAGOV & AUSTIN KOSNIKOWSKI   
  //   Choose what set are you checking if it contains the value
  //   Choose what set do you want to get the value from
  //   Choose the set to output the older block; Use OlderTagDirty to determine if it needs to be written to the Mem
  //   Probably will need for the FSM
endmodule

module Set (
  input  ClkIn,
  input  InitIn,
  input  [6:0] CPUTag,
  input  [1:0] CPUOffset,
  input  [31:0] BlockFromMem,
  input  [7:0] CPUValue,
  input  WriteFrom,
  input  WayWriteEnable,
  input  UpdateAgesEnable,
  output contains,
  output [7:0] ByteReadOut,
  output [6:0] OlderTagOut,
  output OlderTagDirtyOut,
  output [31:0] OlderBlockOut
);

  wire comparator_4_gt, comparator_4_lt, comparator_5_gt, comparator_6_gt, contains0, contains1, contains2,
       DirtyWay0, DirtyWay1, DirtyWay2, WayWriteEneable0, WayWriteEneable1, WayWriteEneable2;
  wire [1:0] adder_1_out, adder_2_out, adder_3_out, AgeIn0, AgeIn1, AgeIn2, AgeOfWayAccessed, AgeWay0,
       AgeWay1, AgeWay2, MatchAt, multiplexer_1_out, multiplexer_3_out, multiplexer_4_out, multiplexer_6_out,
       WayContains, WayOlder;
  wire [2:0] and_1_out, comparator_1_gt, comparator_2_gt, comparator_3_gt, comparator_7_eq;
  wire [6:0] WayTagOut0, WayTagOut1, WayTagOut2;
  wire [7:0] ByteReadOut0, ByteReadOut1, ByteReadOut2, CPUVal0, CPUVal1, CPUVal2;
  wire [31:0] Block0, Block1, Block2, BlockIn0, BlockIn1, BlockIn2;

  Demultiplexer #(.enable("false"), .select(2), .width(32)) demultiplexer_1 (
    .out0(BlockIn0), .out1(BlockIn1), .out2(BlockIn2), .in(BlockFromMem), .sel(WayOlder));  // open: out3
  Demultiplexer #(.enable("false"), .select(2), .width(8)) demultiplexer_2 (
    .out0(CPUVal0), .out1(CPUVal1), .out2(CPUVal2), .in(CPUValue), .sel(WayContains));  // open: out3
  Multiplexer #(.enable("false"), .width(2)) multiplexer_1 (
    .in0(WayOlder), .in1(WayContains), .out(multiplexer_1_out), .sel(WriteFrom));
  Demultiplexer #(.enable("false"), .select(2)) demultiplexer_3 (
    .out0(WayWriteEneable0), .out1(WayWriteEneable1), .out2(WayWriteEneable2), .in(WayWriteEnable),
    .sel(multiplexer_1_out));  // open: out3
  Multiplexer #(.enable("false"), .select(2), .width(2)) multiplexer_2 (
    .in0(AgeWay0), .in1(AgeWay1), .in2(AgeWay2), .out(AgeOfWayAccessed), .sel(WayContains));  // open: in3
  Adder #(.width(2)) adder_1 (.a(AgeWay0), .b(2'b01), .out(adder_1_out));  // open: cin, cout
  Adder #(.width(2)) adder_2 (.a(AgeWay1), .b(2'b01), .out(adder_2_out));  // open: cin, cout
  Adder #(.width(2)) adder_3 (.a(AgeWay2), .b(2'b01), .out(adder_3_out));  // open: cin, cout
  Comparator #(.mode("unsigned"), .width(2)) comparator_1 (
    .a(AgeWay0), .b(AgeOfWayAccessed), .gt(comparator_1_gt[0]), .eq(comparator_1_gt[1]),
    .lt(comparator_1_gt[2]));
  Comparator #(.mode("unsigned"), .width(2)) comparator_2 (
    .a(AgeWay1), .b(AgeOfWayAccessed), .gt(comparator_2_gt[0]), .eq(comparator_2_gt[1]),
    .lt(comparator_2_gt[2]));
  Comparator #(.mode("unsigned"), .width(2)) comparator_3 (
    .a(AgeWay2), .b(AgeOfWayAccessed), .gt(comparator_3_gt[0]), .eq(comparator_3_gt[1]),
    .lt(comparator_3_gt[2]));
  Multiplexer #(.enable("false"), .select(3), .width(2)) multiplexer_3 (
    .in1(AgeWay0), .in2(2'b00), .in4(adder_1_out), .out(multiplexer_3_out), .sel(comparator_1_gt));  // open: in0, in3, in5, in6, in7
  Multiplexer #(.enable("false"), .select(3), .width(2)) multiplexer_4 (
    .in1(AgeWay1), .in2(2'b00), .in4(adder_2_out), .out(multiplexer_4_out), .sel(comparator_2_gt));  // open: in0, in3, in5, in6, in7
  Multiplexer #(.enable("false"), .width(2)) multiplexer_5 (
    .in0(multiplexer_4_out), .in1(2'b01), .out(AgeIn1), .sel(InitIn));
  Multiplexer #(.enable("false"), .select(3), .width(2)) multiplexer_6 (
    .in1(AgeWay2), .in2(2'b00), .in4(adder_3_out), .out(multiplexer_6_out), .sel(comparator_3_gt));  // open: in0, in3, in5, in6, in7
  // Probe on AgeIn0
  Multiplexer #(.enable("false"), .width(2)) multiplexer_7 (
    .in0(multiplexer_3_out), .in1(2'b00), .out(AgeIn0), .sel(InitIn));
  // Probe on AgeIn1
  // Probe on AgeIn2
  Multiplexer #(.enable("false"), .width(2)) multiplexer_8 (
    .in0(multiplexer_6_out), .in1(2'b10), .out(AgeIn2), .sel(InitIn));
  Way Way0 (
    .Clk(ClkIn), .CPUTag(CPUTag), .CPUOffset(CPUOffset), .AgeIn(AgeIn0), .BlockFromMem(BlockIn0),
    .WayWriteEnable(WayWriteEneable0), .CPUValue(CPUVal0), .WriteFrom(WriteFrom),
    .UpdateAgeEn(UpdateAgesEnable), .contains(contains0), .ByteReadOut(ByteReadOut0), .DirtyOut(DirtyWay0),
    .WayTagOut(WayTagOut0), .AgeWayOut(AgeWay0), .BlockOut(Block0));
  Way Way1 (
    .Clk(ClkIn), .CPUTag(CPUTag), .CPUOffset(CPUOffset), .AgeIn(AgeIn1), .BlockFromMem(BlockIn1),
    .WayWriteEnable(WayWriteEneable1), .CPUValue(CPUVal1), .WriteFrom(WriteFrom),
    .UpdateAgeEn(UpdateAgesEnable), .contains(contains1), .ByteReadOut(ByteReadOut1), .DirtyOut(DirtyWay1),
    .WayTagOut(WayTagOut1), .AgeWayOut(AgeWay1), .BlockOut(Block1));
  Way Way2 (
    .Clk(ClkIn), .CPUTag(CPUTag), .CPUOffset(CPUOffset), .AgeIn(AgeIn2), .BlockFromMem(BlockIn2),
    .WayWriteEnable(WayWriteEneable2), .CPUValue(CPUVal2), .WriteFrom(WriteFrom),
    .UpdateAgeEn(UpdateAgesEnable), .contains(contains2), .ByteReadOut(ByteReadOut2), .DirtyOut(DirtyWay2),
    .WayTagOut(WayTagOut2), .AgeWayOut(AgeWay2), .BlockOut(Block2));
  BitFinder #(.width(3)) bitfinder_1 (.in({contains2, contains1, contains0}), .index(WayContains), .found(contains));
  // Probe on contains
  // Probe on WayContains
  // Probe on ByteReadOut
  Multiplexer #(.enable("false"), .select(2), .width(8)) multiplexer_9 (
    .in0(ByteReadOut0), .in1(ByteReadOut1), .in2(ByteReadOut2), .out(ByteReadOut), .sel(WayContains));  // open: in3
  Comparator #(.mode("unsigned"), .width(2)) comparator_4 (
    .a(AgeWay0), .b(AgeWay1), .gt(comparator_4_gt), .lt(comparator_4_lt));  // open: eq
  Comparator #(.mode("unsigned"), .width(2)) comparator_5 (
    .a(AgeWay0), .b(AgeWay2), .gt(comparator_5_gt), .lt(and_1_out[2]));  // open: eq
  Comparator #(.mode("unsigned"), .width(2)) comparator_6 (
    .a(AgeWay1), .b(AgeWay2), .gt(comparator_6_gt));  // open: eq, lt
  Comparator #(.mode("unsigned"), .width(7)) comparator_7 (
    .a(WayTagOut0), .b(CPUTag), .eq(comparator_7_eq[0]));  // open: gt, lt
  Comparator #(.mode("unsigned"), .width(7)) comparator_8 (
    .a(WayTagOut1), .b(CPUTag), .eq(comparator_7_eq[1]));  // open: gt, lt
  Comparator #(.mode("unsigned"), .width(7)) comparator_9 (
    .a(WayTagOut2), .b(CPUTag), .eq(comparator_7_eq[2]));  // open: gt, lt
  and and_1 (and_1_out[0], comparator_4_gt, comparator_5_gt);
  and and_2 (and_1_out[1], comparator_4_lt, comparator_6_gt);
  BitFinder #(.width(3)) bitfinder_2 (.in(comparator_7_eq), .index(MatchAt));  // open: found
  // Probe on WayOlder
  BitFinder #(.width(3)) bitfinder_3 (.in(and_1_out), .index(WayOlder));  // open: found
  // Probe on MatchAt
  Multiplexer #(.enable("false"), .select(2)) multiplexer_10 (
    .in0(DirtyWay0), .in1(DirtyWay1), .in2(DirtyWay2), .out(OlderTagDirtyOut), .sel(WayOlder));  // open: in3
  Multiplexer #(.enable("false"), .select(2), .width(32)) multiplexer_11 (
    .in0(Block0), .in1(Block1), .in2(Block2), .out(OlderBlockOut), .sel(WayOlder));  // open: in3
  // Probe on OlderTagOut
  Multiplexer #(.enable("false"), .select(2), .width(7)) multiplexer_12 (
    .in0(WayTagOut0), .in1(WayTagOut1), .in2(WayTagOut2), .out(OlderTagOut), .sel(WayOlder));  // open: in3

  // Other names for the same wires on the sheet: BlockIn[31:0] = BlockFromMem; Clk = ClkIn; CPUVal[7:0] = CPUValue;
  //   Initialize = InitIn; OlderBlock[31:0] = OlderBlockOut; UpdateAges = UpdateAgesEnable;
  //   WayOlderDirty = OlderTagDirtyOut; WayTagOlder[6:0] = OlderTagOut; WayWriteEneable = WayWriteEnable

  // Notes on the sheet:
  //   We want to write only from CPU or Memory 
  //   We send the requested block from memory to the older block, which we evict
  //   This  block sends WayWriteEnable to the appropriate Way
  //   This block sends CPUValue to the Way with the same tag and Valid bit
  //   The block bellow deals with the Ages
  //   If we write from CPU(1) then we need to write to the Way what is Valid and Tags match
  //   If we want to write from memory, then we evict and we write to the oldest way
  //   VLADIMIR PLAGOV & AUSTIN KOSNIKOWSKI   
  //   Choose what way should pass its value
  //   Contains?
  //   Looks like we do not need it. We also need to check for the valid bit and WayContains already does that.
  //   What way contains the value?
  //   What way is older?
  //   Which tag Way matches to the CPU Tag?
  //   Check if the older way is dirty
  //   Output the older Tag
  //   Output the older Block
endmodule

module Way (
  input  Clk,
  input  [6:0] CPUTag,
  input  [1:0] CPUOffset,
  input  [1:0] AgeIn,
  input  [31:0] BlockFromMem,
  input  WayWriteEnable,
  input  [7:0] CPUValue,
  input  WriteFrom,
  input  UpdateAgeEn,
  output contains,
  output [7:0] ByteReadOut,
  output DirtyOut,
  output [6:0] WayTagOut,
  output [1:0] AgeWayOut,
  output [31:0] BlockOut
);

  wire comparator_1_eq, demultiplexer_1_out0, demultiplexer_1_out1, demultiplexer_1_out2,
       demultiplexer_1_out3, multiplexer_5_out, multiplexer_6_out, multiplexer_7_out, multiplexer_8_out,
       multiplexer_9_out, WayValid, WE0, WE1, WE2, WE3;
  wire [7:0] ByteIn0, ByteIn1, ByteIn2, ByteIn3;

  Multiplexer #(.enable("false"), .width(8)) multiplexer_1 (
    .in0(BlockFromMem[7:0]), .in1(CPUValue), .out(ByteIn0), .sel(WriteFrom));
  Multiplexer #(.enable("false"), .width(8)) multiplexer_2 (
    .in0(BlockFromMem[15:8]), .in1(CPUValue), .out(ByteIn1), .sel(WriteFrom));
  Multiplexer #(.enable("false"), .width(8)) multiplexer_3 (
    .in0(BlockFromMem[23:16]), .in1(CPUValue), .out(ByteIn2), .sel(WriteFrom));
  Multiplexer #(.enable("false"), .width(8)) multiplexer_4 (
    .in0(BlockFromMem[31:24]), .in1(CPUValue), .out(ByteIn3), .sel(WriteFrom));
  Register #(.width(7)) Tag (.D(CPUTag), .en(WayWriteEnable), .clk(Clk), .Q(WayTagOut));  // open: clr
  Register #(.width(1)) Valid (.D(1'b1), .en(WayWriteEnable), .clk(Clk), .Q(WayValid));  // open: clr
  Register #(.width(1)) Dirty (.D(multiplexer_5_out), .en(WayWriteEnable), .clk(Clk), .Q(DirtyOut));  // open: clr
  Multiplexer #(.enable("false")) multiplexer_5 (.in0(1'b0), .in1(1'b1), .out(multiplexer_5_out), .sel(WriteFrom));
  Register #(.width(2)) Age (.D(AgeIn), .en(UpdateAgeEn), .clk(Clk), .Q(AgeWayOut));  // open: clr
  Demultiplexer #(.enable("false"), .select(2)) demultiplexer_1 (
    .out0(demultiplexer_1_out0), .out1(demultiplexer_1_out1), .out2(demultiplexer_1_out2),
    .out3(demultiplexer_1_out3), .in(WayWriteEnable), .sel(CPUOffset));
  Register Byte0 (.D(ByteIn0), .en(WE0), .clk(Clk), .Q(BlockOut[7:0]));  // open: clr
  Register Byte2 (.D(ByteIn2), .en(WE2), .clk(Clk), .Q(BlockOut[23:16]));  // open: clr
  Comparator #(.width(7)) comparator_1 (.a(CPUTag), .b(WayTagOut), .eq(comparator_1_eq));  // open: gt, lt
  Multiplexer #(.enable("false")) multiplexer_6 (
    .in0(1'b1), .in1(demultiplexer_1_out0), .out(multiplexer_6_out), .sel(WriteFrom));
  Multiplexer #(.enable("false")) multiplexer_7 (
    .in0(1'b1), .in1(demultiplexer_1_out1), .out(multiplexer_7_out), .sel(WriteFrom));
  Multiplexer #(.enable("false")) multiplexer_8 (
    .in0(1'b1), .in1(demultiplexer_1_out2), .out(multiplexer_8_out), .sel(WriteFrom));
  Multiplexer #(.enable("false")) multiplexer_9 (
    .in0(1'b1), .in1(demultiplexer_1_out3), .out(multiplexer_9_out), .sel(WriteFrom));
  and and_1 (contains, comparator_1_eq, WayValid);
  Register Byte1 (.D(ByteIn1), .en(WE1), .clk(Clk), .Q(BlockOut[15:8]));  // open: clr
  Register Byte3 (.D(ByteIn3), .en(WE3), .clk(Clk), .Q(BlockOut[31:24]));  // open: clr
  and and_2 (WE0, multiplexer_6_out, WayWriteEnable);
  and and_3 (WE1, multiplexer_7_out, WayWriteEnable);
  and and_4 (WE2, multiplexer_8_out, WayWriteEnable);
  and and_5 (WE3, multiplexer_9_out, WayWriteEnable);
  Multiplexer #(.enable("false"), .select(2), .width(8)) multiplexer_10 (
    .in0(BlockOut[7:0]), .in1(BlockOut[15:8]), .in2(BlockOut[23:16]), .in3(BlockOut[31:24]),
    .out(ByteReadOut), .sel(CPUOffset));

  // Other names for the same wires on the sheet: Age[1:0] = AgeWayOut; ByteMem0[7:0] = BlockFromMem[7:0];
  //   ByteMem1[7:0] = BlockFromMem[15:8]; ByteMem2[7:0] = BlockFromMem[23:16]; ByteMem3[7:0] = BlockFromMem[31:24];
  //   BlockToWrite[31:0] = BlockOut; Byte0[7:0] = BlockOut[7:0]; Byte1[7:0] = BlockOut[15:8];
  //   Byte2[7:0] = BlockOut[23:16]; Byte3[7:0] = BlockOut[31:24]; CPUVal[7:0] = CPUValue; Dirty = DirtyOut;
  //   UpdateAge = UpdateAgeEn; WayTag[6:0] = WayTagOut; WWE = WayWriteEnable

  // Notes on the sheet:
  //   1-from CPU; 0-from Memory. Probably will be handled by the FSM
  //   Write Enable bit. 1-write from CPU or Memory
  //   VLADIMIR PLAGOV & AUSTIN KOSNIKOWSKI   
endmodule

module Next_State_FSM (
  input  S2,
  input  S1,
  input  S0,
  input  CpuRead,
  input  CpuWrite,
  input  DidContain,
  input  OlderTagDirty,
  output S2_Next,
  output S1_Next,
  output S0_Next
);

  wire and_1_out, and_2_out, and_3_out, and_4_out, and_5_out, and_6_out, and_7_out, and_8_out, and_9_out,
       and_10_out, and_11_out, and_12_out, and_13_out, and_14_out, not_1_out, not_2_out, not_3_out,
       not_4_out, not_5_out, not_6_out;

  not not_1 (not_1_out, S2);
  not not_2 (not_2_out, S1);
  not not_3 (not_3_out, S0);
  not not_4 (not_4_out, CpuRead);
  not not_5 (not_5_out, CpuWrite);
  not not_6 (not_6_out, OlderTagDirty);
  and and_1 (and_1_out, S1, not_4_out, CpuWrite, not_6_out);
  and and_2 (and_2_out, S1, not_4_out, CpuWrite, DidContain);
  and and_3 (and_3_out, not_1_out, S1, CpuRead, not_5_out, not_6_out);
  and and_4 (and_4_out, not_1_out, S1, CpuRead, not_5_out, DidContain);
  and and_5 (and_5_out, not_1_out, S1, S0);
  and and_6 (and_6_out, S2, not_3_out);
  and and_7 (and_7_out, S2, S1, not_4_out);
  and and_8 (and_8_out, not_1_out, S0);
  and and_9 (and_9_out, S1, not_3_out);
  and and_10 (and_10_out, not_2_out, not_3_out);
  and and_11 (and_11_out, not_3_out, not_4_out, CpuWrite, OlderTagDirty);
  and and_12 (and_12_out, not_3_out, not_4_out, CpuWrite, DidContain);
  and and_13 (and_13_out, not_3_out, CpuRead, not_5_out, OlderTagDirty);
  and and_14 (and_14_out, not_3_out, CpuRead, not_5_out, DidContain);
  or or_1 (S2_Next, and_1_out, and_2_out, and_3_out, and_4_out, and_5_out, and_6_out, and_7_out);
  or or_2 (S1_Next, and_8_out, and_9_out);
  or or_3 (S0_Next, and_10_out, and_11_out, and_12_out, and_13_out, and_14_out, S2);

  // Notes on the sheet:
  //   VLADIMIR PLAGOV & AUSTIN KOSNIKOWSKI   
endmodule

module FSM_Output (
  input  S2,
  input  S1,
  input  S0,
  input  CpuRead,
  input  CpuWrite,
  input  DidContain,
  input  OlderTagDirty,
  output Initialize,
  output Ready,
  output MemRead,
  output MemWrite,
  output WayWriteEnable,
  output WriteFrom,
  output UpdateAges
);

  wire and_3_out, and_4_out, and_5_out, and_6_out, and_7_out, and_8_out, and_9_out, and_11_out, and_12_out,
       not_1_out, not_2_out, not_3_out, not_4_out, not_5_out, not_6_out;

  not not_1 (not_1_out, S2);
  not not_2 (not_2_out, S1);
  not not_3 (not_3_out, S0);
  not not_4 (not_4_out, CpuRead);
  not not_5 (not_5_out, CpuWrite);
  not not_6 (not_6_out, DidContain);
  and and_1 (Initialize, not_1_out, not_2_out, not_3_out);
  and and_2 (Ready, not_1_out, not_2_out, S0);
  and and_3 (and_3_out, S2, S1, not_3_out, not_4_out, CpuWrite, not_6_out);
  and and_4 (and_4_out, S2, S1, not_3_out, CpuRead, not_5_out, not_6_out);
  and and_5 (and_5_out, not_1_out, S1, S0, not_4_out, CpuWrite, not_6_out, OlderTagDirty);
  and and_6 (and_6_out, not_1_out, S1, S0, CpuRead, not_5_out, not_6_out, OlderTagDirty);
  and and_7 (and_7_out, S2, not_2_out, S0, not_4_out, CpuWrite);
  and and_8 (and_8_out, S2, S1, not_3_out, not_4_out, CpuWrite, not_6_out);
  and and_9 (and_9_out, S2, S1, not_3_out, CpuRead, not_5_out, not_6_out);
  and and_10 (WriteFrom, S2, not_2_out, S0, not_4_out, CpuWrite);
  and and_11 (and_11_out, not_1_out, not_2_out, not_3_out);
  and and_12 (and_12_out, S2, S1, S0);
  or or_1 (MemRead, and_3_out, and_4_out);
  or or_2 (MemWrite, and_5_out, and_6_out);
  or or_3 (WayWriteEnable, and_7_out, and_8_out, and_9_out);
  or or_4 (UpdateAges, and_11_out, and_12_out);

  // Notes on the sheet:
  //   VLADIMIR PLAGOV & AUSTIN KOSNIKOWSKI   
endmodule
